// Digital circuit example.dig as structural Verilog
module example (
  input  clk,
  input  [31:0] in_13,
  input  in_14,
  input  in_15,
  input  in_16,
  input  in_17,
  input  in_18,
  input  in_19,
  input  in_20,
  input  in_21,
  input  in_22,
  output [31:0] out_2,
  output [31:0] out_3,
  output [31:0] out_4,
  output [31:0] out_5,
  output [31:0] out_6,
  output [31:0] out_7,
  output [31:0] out_8,
  output [31:0] out_9,
  output [31:0] out_10,
  output [31:0] out_11,
  output out_12
);

  wire _0_p3, _0_p4, _0_p6, _0_p7, _1_p4, _1_p5, _1_p8, _1_p9, _2_p4, _2_p5, _2_p6, _2_p9, _2_p10, _2_p11,
       _3_p4, _3_p5, _3_p8, _3_p9, _4_p4, _4_p7, _5_p6, _5_p11, _6_p4, _6_p5, _6_p7, _6_p9, _7_p6, _7_p10;

  // node_module #(.generic("edge_weights := [4,8]; neighbourhood_size := 2;")) _0: pin names not known; wires that end beside it: in_14, clk, _0_p3, _0_p4, out_2, _0_p6, _0_p7
  // node_module #(.generic("edge_weights := [4,8,11]; neighbourhood_size := 3;")) _1: pin names not known; wires that end beside it: in_15, clk, _0_p6, _1_p4, _1_p5, out_3, _0_p3, _1_p8, _1_p9
  // node_module #(.generic("edge_weights := [8,7,4,2]; neighbourhood_size := 4;")) _2: pin names not known; wires that end beside it: in_16, clk, _1_p8, _2_p4, _2_p5, _2_p6, out_4, _1_p4, _2_p9, _2_p10, _2_p11
  // node_module #(.generic("edge_weights := [7, 9, 14]; neighbourhood_size := 3;")) _3: pin names not known; wires that end beside it: in_17, clk, _2_p9, _3_p4, _3_p5, out_5, _2_p4, _3_p8, _3_p9
  // node_module #(.generic("edge_weights := [9,10]; neighbourhood_size := 2;")) _4: pin names not known; wires that end beside it: in_22, clk, _3_p8, _4_p4, out_6, _3_p4, _4_p7
  // node_module #(.generic("edge_weights := [4, 14, 10, 2]; neighbourhood_size := 4;")) _5: pin names not known; wires that end beside it: in_18, clk, _2_p10, _3_p9, _4_p7, _5_p6, out_7, _2_p5, _3_p5, _4_p4, _5_p11
  // node_module #(.generic("edge_weights := [ 6, 2, 1]; neighbourhood_size := 3;")) _6: pin names not known; wires that end beside it: in_19, clk, _5_p11, _6_p4, _6_p5, out_8, _6_p7, _5_p6, _6_p9
  // node_module #(.generic("edge_weights := [8,11, 7,1]; neighbourhood_size := 4;")) _7: pin names not known; wires that end beside it: in_20, clk, _0_p7, _1_p9, _6_p9, _7_p6, out_9, _0_p4, _1_p5, _7_p10, _6_p4
  // node_module #(.generic("edge_weights := [2, 6, 7]; neighbourhood_size := 3;")) _8: pin names not known; wires that end beside it: in_21, clk, _2_p11, _6_p7, _7_p10, out_10, _2_p6, _6_p5, _7_p6
  // final_finder #(.generic("in_nodes := 9;")) final_finder_1: pin names not known; wires that end beside it: in_13, out_2, out_3, out_4, out_5, out_6, out_7, out_8, out_9, out_10, out_11
  final_checker #(.generic("maxValue := 9-1;")) final_checker_1 (.C(clk), .out(out_12));
endmodule
