// Digital circuit node_module.dig as structural Verilog
module node_module (
  input  start,
  input  clock,
  output [31:0] own
);

  wire [31:0] cheapselector_1_out, lookuptable_1_out;

  wires_in #(.generic("in_nodes := args.neighbourhood_size;")) wires_in_1 ();
  LookUpTable #(.Bits(32)) lookuptable_1 (.in0(start), .in1(start), .out(lookuptable_1_out));
  cheapSelector cheapselector_1 (.a(lookuptable_1_out), .out(cheapselector_1_out));  // open: b
  decreasing_mem decreasing_mem_1 (.clock(clock), .A(cheapselector_1_out), .\output (own));
  wires_out #(.generic("out_nodes := args.neighbourhood_size; weights := args.edge_weights;")) wires_out_1 (.IN1(own));

  // Notes on the sheet:
  //   clock: Hz: 50000
  //   contents of lookuptable_1 (hex, n*v repeats v):
  //   7ffffff1
endmodule

/* Code that sets the parameters or builds the circuit:
neighbourhood_size:=6;
edge_weights:=[1,1,1,1,1,1];
*/

/* Code that sets the parameters or builds the circuit:
x_output_start := 33;
y_output_start := 8;
y_output_add:= 1;

x_input_start := 4;
y_input_start := 6;
y_input_add:= 1;

y_input_offset:=0;

for (i:=0;i<args.neighbourhood_size;i++){
    output:=addComponent("Out",x_output_start,y_output_start+i*y_output_add);
    output.Bits=32;
    output.Label="O"+i;
}

for (i:=0;i<args.neighbourhood_size;i++){
    if(args.neighbourhood_size%2=0)
    {
	if(i>=args.neighbourhood_size/2){
	   y_input_offset = 1;
	}
    }
    output:=addComponent("In",x_input_start,y_input_start+i*y_input_add + y_input_offset);
    output.Bits=32;
    output.Label="I"+i;
}

addWire(x_input_start+3,y_input_start + args.neighbourhood_size/2,15,10);
*/
