// Digital circuit decreasing_mem.dig as structural Verilog
module decreasing_mem (
  input  clk,
  input  [31:0] in,
  input  set,
  input  clr,
  output [31:0] out
);

  wire comp_eq, comp_gt, comp_lt;
  wire [31:0] d_ff_as_1_nq, multiplexer_1_out;

  Comparator #(.Bits(32)) comp (.a(in), .b(out), .gt(comp_gt), .eq(comp_eq), .lt(comp_lt));
  Multiplexer #(.Bits(32)) multiplexer_1 (.sel(comp_lt), .in_0(out), .in_1(in), .out(multiplexer_1_out));
  D_FF_AS #(.Bits(32), .Default(2000000)) d_ff_as_1 (
    .Set(set), .D(multiplexer_1_out), .C(clk), .Clr(clr), .Q(out), .nQ(d_ff_as_1_nq));

  // Notes on the sheet:
  //   clk: Hz: 80000
  //   in: default 2147483647
endmodule

/* Test case:
clk clr set in out

############################

0 1 0 10 0

C 0 0 10 0

C 0 1 10 4294967295

C 0 0 10 10

C 0 0 50 10

C 0 1 50 4294967295

C 0 0 50 50

C 0 0 10 10
*/
